# Fritzing sketch mirror (saved by Fritzing 0.9.0b)
breadboards: 1

parts:
  Bauteil2 = Arduino Nano (Rev3.0)
  Bauteil3 = Breakout Board for Electret Microphone
  Grid-Eye = Header 4 [package=jst-4-pth]
  U1 = 74VHC4052 [package=tssop16]
  Bauteil4 = SRF05 Ultrasonic Rangefinder
  LED-Strip = Header 4 [package=jst-4-pth]
  J1 = Piezo Speaker

nets:
  GND: Bauteil2.GND, Bauteil3.GND, Grid-Eye.1, LED-Strip.1
  N1: Bauteil2.D2, U1.Y0
  N2: Bauteil2.D3, U1.VEE
  N3: Bauteil2.D4, U1.A
  N4: Bauteil2.D5, U1.X2
  N5: Bauteil2.D7, Bauteil4.Echo
  N6: Bauteil2.D8, Bauteil4.Trig
  N7: Bauteil2.D11/MOSI, LED-Strip.2
  5V: Bauteil2.5V, Bauteil3.VCC, Grid-Eye.4, LED-Strip.4
  N8: Bauteil2.A6, Bauteil3.AUD
  N9: Bauteil2.A5, Grid-Eye.3
  N10: Bauteil2.A4, Grid-Eye.2
  3V3: Bauteil2.3V3, U1.VCC
  N11: Bauteil2.D13/SCK, LED-Strip.3
  N12: U1.Y3, J1.pin2
  N13: U1.Y1, J1.pin1
