# Fritzing sketch mirror (saved by Fritzing 0.8.7b)
breadboards: 1

parts:
  Bauteil1 = Arduino Uno (Rev3)
  JP1 = Header 4 [package=1x04-1mm-ra]

nets:
  N1: Bauteil1.D11_PWM/MOSI, JP1.3
  N2: Bauteil1.D13/SCK, JP1.2
  N3: Bauteil1.GND, JP1.4
