# Fritzing sketch showers (saved by Fritzing 0.8.7b)
breadboards: 1

parts:
  X1 = Sonar
  X2 = Sonar
  X3 = Sonar
  X4 = Sonar
  LED2 = LED - 5mm [color="Red (633nm)" package="5 mm [THT]"]
  LED3 = LED - 5mm [color="Red (633nm)" package="5 mm [THT]"]
  LED4 = LED - 5mm [color="Red (633nm)" package="5 mm [THT]"]
  LED5 = LED - 5mm [color="Red (633nm)" package="5 mm [THT]"]
  Bauteil1 = Arduino Uno (Rev3)
  LED6 = LED - 5mm [color="Red (633nm)" package="5 mm [THT]"]

nets:
  N1: X1.+5, X2.+5, X3.+5, X4.+5, Bauteil1.5V
  N2: X1.SDA, X2.SDA, X3.SDA, X4.SDA, Bauteil1.A4/SDA
  N3: X1.SCL, X2.SCL, X3.SCL, X4.SCL, Bauteil1.A5/SCL
  GND: X1.GND, X2.GND, X3.GND, X4.GND, LED2.cathode, LED3.cathode, LED4.cathode, LED5.cathode, Bauteil1.GND, LED6.cathode
  N4: LED2.anode, LED3.anode, LED4.anode, LED5.anode, Bauteil1.D2
  N5: Bauteil1.D4, LED6.anode

custom parts:
  Sonar: Devantech SRF08 sonar range-finder. I2C interface. Other Devantech sonars similar
